# Fritzing sketch Reflektor (saved by Fritzing 0.8.3b)
breadboards: 3

parts:
  Brain = Arduino Uno (Rev3)  # not connected
  Audio = Arduino Uno (Rev3)  # not connected
  U1 = 74HC595 [package="DIP16 [THT]"]
  U2 = 74HC595 [package="DIP16 [THT]"]
  IC1 = L293D [package=THT]
  IC2 = L293D [package=THT]
  IC3 = L293D [package=THT]
  IC4 = L293D [package=THT]
  U3 = 74HC595 [package="DIP16 [THT]"]
  J5 = screw terminal, 6 pins
  J3 = screw terminal, 6 pins
  J1 = screw terminal, 6 pins
  R1 = Resistor [tolerance=±5% resistance=220 package=THT]
  R2 = Resistor [tolerance=±5% resistance=220 package=THT]
  R3 = Resistor [tolerance=±5% resistance=220 package=THT]
  J12 = Screw terminal - 2 pins [package=THT]
  J13 = male pin header, 8 pins [form="♂ (male)"]
  J14 = male pin header, 8 pins [form="♂ (male)"]
  J7 = screw terminal, 6 pins
  J16 = male pin header, 6 pins [form="♂ (male)"]
  J17 = screw terminal, 4 pins
  J18 = screw terminal, 4 pins
  R4 = Resistor [tolerance=±5% resistance=220 package=THT]
  R5 = Resistor [tolerance=±5% resistance=220 package=THT]
  R6 = Resistor [tolerance=±5% resistance=220 package=THT]
  R7 = Resistor [tolerance=±5% resistance=220 package=THT]
  R8 = Resistor [tolerance=±5% resistance=220 package=THT]
  R9 = Resistor [tolerance=±5% resistance=220 package=THT]
  R10 = Resistor [tolerance=±5% resistance=220 package=THT]
  J10 = Screw terminal - 2 pins [package=THT]
  J11 = Screw terminal - 2 pins [package=THT]
  J20 = screw terminal, 5 pins
  J9 = screw terminal, 4 pins
  J19 = screw terminal, 6 pins
  U4 = Voltage Regulator - 9V [package="TO220 [THT]"]
  J21 = male pin header, 6 pins [form="♂ (male)"]
  J22 = male pin header, 6 pins [form="♂ (male)"]
  J23 = male pin header, 6 pins [form="♂ (male)"]

nets:
  N1: U1.Q1, IC2.In_2
  N2: U1.Q2, IC2.In_1
  N3: U1.Q3, IC2.In_4
  N4: U1.Q4, IC1.In_3
  N5: U1.Q5, IC1.In_2
  N6: U1.Q6, IC1.In_1
  N7: U1.Q7, IC1.In_4
  GND: U1.GND, U1.OE, U2.GND, U2.OE, IC1.0V, IC2.0V, IC3.0V, IC4.0V, U3.GND, U3.OE, J5.pin6, J3.pin6, J1.pin6, J12.pin1, J7.pin6, J17.pin4, J18.pin4, R4.Pin_1, R5.Pin_1, J10.pin2, J11.pin2, J20.pin5, J9.pin2, J9.pin4, J19.pin2, U4.GND, J23.pin4
  N8: U1.Q7', U3.DS
  VCC: U1.MR, U1.VCC, U2.MR, U2.VCC, IC1.Enable_1, IC1.Enable_2, IC1.+V, IC2.Enable_1, IC2.+Vmotor, IC2.Enable_2, IC2.+V, IC3.Enable_1, IC3.+Vmotor, IC3.Enable_2, IC3.+V, IC4.Enable_1, IC4.+Vmotor, IC4.Enable_2, IC4.+V, U3.MR, U3.VCC, J17.pin1, J18.pin1, J10.pin1, J19.pin6, J22.pin3, J22.pin4, J23.pin3
  N9: U1.SH_CP, U2.SH_CP, U3.SH_CP, J13.pin6, J19.pin3
  N10: U1.ST_CP, U2.ST_CP, U3.ST_CP, J13.pin4
  N11: U1.DS, U2.Q7'
  N12: U1.Q0, IC2.In_3
  N13: U2.Q1, IC4.In_2
  N14: U2.Q2, IC4.In_1
  N15: U2.Q3, IC4.In_4
  N16: U2.Q4, IC3.In_3
  N17: U2.Q5, IC3.In_2
  N18: U2.Q6, IC3.In_1
  N19: U2.Q7, IC3.In_4
  N20: U2.Q0, IC4.In_3
  N21: IC1.Out_1_(_Controlled_by_Enable_1_), J7.pin2
  N22: IC1.Out_2_(_Controlled_by_Enable_1_), J7.pin3
  N23: IC1.+Vmotor, J12.pin2, J11.pin1, U4.input_voltage
  N24: IC1.Out_3_(_Controlled_by_Enable_2_), J7.pin4
  N25: IC1.Out_4_(_Controlled_by_Enable_2_), J7.pin1
  N26: IC2.Out_1_(_Controlled_by_Enable_1_), J1.pin2
  N27: IC2.Out_2_(_Controlled_by_Enable_1_), J1.pin3
  N28: IC2.Out_3_(_Controlled_by_Enable_2_), J1.pin4
  N29: IC2.Out_4_(_Controlled_by_Enable_2_), J1.pin1
  N30: IC3.Out_1_(_Controlled_by_Enable_1_), J3.pin2
  N31: IC3.Out_2_(_Controlled_by_Enable_1_), J3.pin3
  N32: IC3.Out_3_(_Controlled_by_Enable_2_), J3.pin4
  N33: IC3.Out_4_(_Controlled_by_Enable_2_), J3.pin1
  N34: IC4.Out_1_(_Controlled_by_Enable_1_), J5.pin2
  N35: IC4.Out_2_(_Controlled_by_Enable_1_), J5.pin3
  N36: IC4.Out_3_(_Controlled_by_Enable_2_), J5.pin4
  N37: IC4.Out_4_(_Controlled_by_Enable_2_), J5.pin1
  N38: U3.Q1, R2.Pin_1
  N39: U3.Q2, R3.Pin_1
  N40: U3.Q3, R7.Pin_1
  N41: U3.Q4, R6.Pin_1
  N42: U3.Q5, R10.Pin_1
  N43: U3.Q6, R9.Pin_1
  N44: U3.Q7, R8.Pin_0
  N45: U3.Q0, R1.Pin_1
  N46: J5.pin5, R1.Pin_0
  N47: J3.pin5, R2.Pin_0
  N48: J1.pin5, R3.Pin_0
  N49: J13.pin5, J19.pin5
  N50: J13.pin7, J19.pin4
  N51: J14.pin1, J7.pin5
  N52: J14.pin2, J20.pin1
  N53: J14.pin3, J20.pin2
  N54: J14.pin4, J20.pin3
  N55: J16.pin3, J17.pin2, R4.Pin_0
  N56: J16.pin4, J18.pin2, R5.Pin_0
  N57: J16.pin5, J21.pin5
  N58: J16.pin6, J21.pin6
  N59: J17.pin3, R6.Pin_0
  N60: J18.pin3, R7.Pin_0
  N61: R8.Pin_1, J20.pin4
  N62: R9.Pin_0, J9.pin1
  N63: R10.Pin_0, J9.pin3
  N64: J19.pin1, U4.output_voltage

notes:
  Stepper carrito (12v)
  y su fin de carrera
  Input 12v
  Input 5v
  12v
  (ampli)
  Display 16 segmentos
  Botonera y LED ganaste
  Steppers de espejos 1, 2, 3 (5v)
  y sus LEDS
  LDRs y sus leds
  LEDs extra
  12v!
  7809, 9v
  Lógica de juego
  Coprocesador de Audio (waveshield)
  Reflektor

custom parts:
  Voltage Regulator - 9V: 9V DC Voltage Regulator
