# Fritzing sketch display16 (saved by Fritzing 0.8.3b)
perfboards: 1

parts:
  U1 = Alphanumeric LED Display [package=alphanumeric]
  R12 = Resistor [tolerance=±5% resistance=470 package=THT]
  R11 = Resistor [tolerance=±5% resistance=470 package=THT]
  R10 = Resistor [tolerance=±5% resistance=470 package=THT]
  R13 = Resistor [tolerance=±5% resistance=470 package=THT]
  R15 = Resistor [tolerance=±5% resistance=470 package=THT]
  R14 = Resistor [tolerance=±5% resistance=470 package=THT]
  R5 = Resistor [tolerance=±5% resistance=390 package=THT]
  R8 = Resistor [tolerance=±5% resistance=390 package=THT]
  R9 = Resistor [tolerance=±5% resistance=390 package=THT]
  R7 = Resistor [tolerance=±5% resistance=390 package=THT]
  R6 = Resistor [tolerance=±5% resistance=390 package=THT]
  R2 = Resistor [tolerance=±5% resistance=390 package=THT]
  R4 = Resistor [tolerance=±5% resistance=390 package=THT]
  R3 = Resistor [tolerance=±5% resistance=390 package=THT]
  R16 = Resistor [tolerance=±5% resistance=390 package=THT]
  R1 = Resistor [tolerance=±5% resistance=390 package=THT]
  J1 = screw terminal, 6 pins
  J2 = screw terminal, 6 pins
  IC1 = IC, DIP package, 22 pins [chip_label=MM5484N]

nets:
  N1: U1.A1, R15.Pin_0
  N2: U1.H, R4.Pin_0
  N3: U1.F, R3.Pin_0
  N4: U1.VCC, J1.pin1, J2.pin6
  N5: U1.G1, R14.Pin_0
  N6: U1.E, R2.Pin_0
  N7: U1.D1, R13.Pin_0
  N8: U1.N, R1.Pin_0
  N9: U1.M, R16.Pin_0
  N10: U1.D2, R12.Pin_1
  N11: U1.L, R9.Pin_1
  N12: U1.C, R8.Pin_1
  N13: U1.G2, R11.Pin_1
  N14: U1.B, R7.Pin_1
  N15: U1.A2, R10.Pin_1
  N16: U1.K, R6.Pin_1
  N17: U1.J, R5.Pin_1
  N18: R12.Pin_0, IC1.pin22
  N19: R11.Pin_0, IC1.pin21
  N20: R10.Pin_0, IC1.pin20
  N21: R13.Pin_1, IC1.pin1
  N22: R15.Pin_1, IC1.pin3
  N23: R14.Pin_1, IC1.pin2
  N24: R5.Pin_0, IC1.pin12
  N25: R8.Pin_0, IC1.pin15
  N26: R9.Pin_0, IC1.pin19
  N27: R7.Pin_0, IC1.pin14
  N28: R6.Pin_0, IC1.pin13
  N29: R2.Pin_1, IC1.pin9
  N30: R4.Pin_1, IC1.pin11
  N31: R3.Pin_1, IC1.pin10
  N32: R16.Pin_1, IC1.pin4
  N33: R1.Pin_1, IC1.pin8
  N34: J1.pin2, J2.pin5, IC1.pin6
  N35: J1.pin3, J2.pin4, IC1.pin16
  N36: J1.pin4, J2.pin3, IC1.pin18
  N37: J1.pin5, J2.pin2, IC1.pin17
  N38: J1.pin6, IC1.pin7
  N39: J2.pin1, IC1.pin5

notes:
  data in
  enable
  clock
  ground
  5v
  9v
  DATA_IN
  CLOCK
  ENABLE
  GND
  5V
  9V
  DATA_OUT
