# Fritzing sketch protoflektor (saved by Fritzing 0.8.3b)
stripboards: 1

parts:
  IC4 = L293D [package=THT]
  U3 = 74HC595 SMD [package="SO16 [SMD]"]
  J1 = female pin header, 6 pins [form="♀ (female)"]
  IC5 = L293D [package=THT]
  J2 = female pin header, 6 pins [form="♀ (female)"]
  J3 = male pin header, 3 pins [form="♂ (male)"]
  J4 = male pin header, 3 pins [form="♂ (male)"]
  IC6 = L293D [package=THT]  # not connected
  IC7 = L293D [package=THT]  # not connected
  U4 = 74HC595 SMD [package="SO16 [SMD]"]  # not connected
  J5 = female pin header, 6 pins [form="♀ (female)"]  # not connected
  J6 = female pin header, 6 pins [form="♀ (female)"]  # not connected
  J7 = male pin header, 3 pins [form="♂ (male)"]  # not connected
  J8 = male pin header, 3 pins [form="♂ (male)"]  # not connected

nets:
  N1: IC4.Enable_1, IC4.In_1, IC4.Enable_2, IC4.In_3, IC4.In_4, IC4.+V, U3.Q2, U3.Q3, U3.Q6, U3.Q7, U3.MR, U3.Q0, U3.VCC, IC5.Enable_1, IC5.In_1, IC5.Enable_2, IC5.In_4, IC5.+V, J4.pin3
  N2: IC4.Out_1_(_Controlled_by_Enable_1_), J1.pin4
  N3: IC4.0V, IC4.Out_3_(_Controlled_by_Enable_2_), IC4.Out_4_(_Controlled_by_Enable_2_), U3.GND, U3.OE, J1.pin1, J1.pin2, J1.pin3, J1.pin6, IC5.0V, IC5.Out_2_(_Controlled_by_Enable_1_), J2.pin2, J2.pin5
  N4: IC4.Out_2_(_Controlled_by_Enable_1_), J1.pin5
  N5: IC4.In_2, IC4.+Vmotor, U3.Q1, J3.pin1, J4.pin1, J4.pin2
  N6: U3.Q4, IC5.In_3
  N7: U3.Q5, IC5.In_2, IC5.+Vmotor, J3.pin2
  N8: IC5.Out_1_(_Controlled_by_Enable_1_), J2.pin4
  N9: IC5.Out_3_(_Controlled_by_Enable_2_), J2.pin6
  N10: IC5.Out_4_(_Controlled_by_Enable_2_), J2.pin3
